// Logisim project 19070001001_Lab12_s2.circ as structural Verilog: 1 circuit, main circuit main
module main (
  input  [7:0] in_1,
  input  [7:0] in_2,
  input  in_3,
  input  in_4,
  output [15:0] out_5,
  output out_6,
  output out_7,
  output out_8,
  output out_9,
  output out_10
);

  wire and_1_out, clock_1_out, clock_2_out, d_ff_1_qn, d_ff_2_qn, d_ff_3_qn, d_ff_4_qn, d_ff_5_qn, not_1_out,
       not_2_out, shift_register_1_out;
  wire [7:0] multiplexer_1_out, shift_register_2_q7, shift_register_2_q15;

  Clock clock_1 (.out(clock_1_out));
  Multiplexer #(.width(8), .enable("false")) multiplexer_1 (
    .in0(in_1), .in1(in_2), .out(multiplexer_1_out), .sel(in_3));
  Shift_Register shift_register_1 (
    .clk(clock_1_out), .out(shift_register_1_out), .load(in_4), .d0(multiplexer_1_out[7]),
    .d1(multiplexer_1_out[6]), .d2(multiplexer_1_out[5]), .d3(multiplexer_1_out[4]),
    .d4(multiplexer_1_out[3]), .d5(multiplexer_1_out[2]), .d6(multiplexer_1_out[1]), .d7(multiplexer_1_out[0]));  // open: shift, in, clr, q0, q1, q2, q3, q4, q5, q6, q7
  not not_1 (not_1_out, in_4);
  and and_1 (and_1_out, not_1_out, clock_1_out);
  Clock clock_2 (.out(clock_2_out));
  D_Flip_Flop d_ff_1 (
    .clk(clock_2_out), .D(d_ff_1_qn), .Q(out_6), .Qn(d_ff_1_qn), .en(not_2_out));  // open: preset, reset
  D_Flip_Flop d_ff_2 (
    .clk(d_ff_1_qn), .D(d_ff_2_qn), .Q(out_7), .Qn(d_ff_2_qn), .en(not_2_out));  // open: preset, reset
  D_Flip_Flop d_ff_3 (
    .clk(d_ff_2_qn), .D(d_ff_3_qn), .Q(out_8), .Qn(d_ff_3_qn), .en(not_2_out));  // open: preset, reset
  D_Flip_Flop d_ff_4 (
    .clk(d_ff_3_qn), .D(d_ff_4_qn), .Q(out_9), .Qn(d_ff_4_qn), .en(not_2_out));  // open: preset, reset
  D_Flip_Flop d_ff_5 (
    .clk(d_ff_4_qn), .D(d_ff_5_qn), .Q(out_10), .Qn(d_ff_5_qn), .en(not_2_out));  // open: preset, reset
  not not_2 (not_2_out, out_10);
  Shift_Register #(.length(16)) shift_register_2 (
    .in(shift_register_1_out), .clk(and_1_out), .q0(shift_register_2_q7[7]), .q1(shift_register_2_q7[6]),
    .q2(shift_register_2_q7[5]), .q3(shift_register_2_q7[4]), .q4(shift_register_2_q7[3]),
    .q5(shift_register_2_q7[2]), .q6(shift_register_2_q7[1]), .q7(shift_register_2_q7[0]),
    .q8(shift_register_2_q15[7]), .q9(shift_register_2_q15[6]), .q10(shift_register_2_q15[5]),
    .q11(shift_register_2_q15[4]), .q12(shift_register_2_q15[3]), .q13(shift_register_2_q15[2]),
    .q14(shift_register_2_q15[1]), .q15(shift_register_2_q15[0]));  // open: shift, out, load, clr, d0, d1, d2, d3, d4, d5, d6, d7, d8, d9, d10, d11, d12, d13, d14, d15
  Multiplier #(.width(16)) multiplier_1 (
    .a({{8{1'b1}}, shift_register_2_q15}), .b({{8{1'b1}}, shift_register_2_q7}), .out(out_5));  // open: cin, cout

  // Notes on the sheet:
  //   19070001001 mod 16 = 4 => 4 + 11 = 15
endmodule
