// Logisim project Labwork8_s2_19070001001.circ as structural Verilog: 2 circuits, main circuit main
module main (
  input  I3,
  input  I2,
  input  I1,
  input  I0,
  input  in_5,
  input  in_6,
  input  in_7,
  input  I3_2,
  input  I2_2,
  input  I1_2,
  input  I0_2,
  output O4,
  output O3,
  output O2,
  output O1,
  output O0
);

  wire n4bit_to_5bit_bcd_2_e, n4bit_to_5bit_bcd_2_w, n4bit_to_5bit_bcd_2_x, n4bit_to_5bit_bcd_2_y,
       n4bit_to_5bit_bcd_2_z, n7_segment_display_driver_1_a_2, n7_segment_display_driver_1_b_2,
       n7_segment_display_driver_1_c_2, n7_segment_display_driver_1_d_2, n7_segment_display_driver_1_e,
       n7_segment_display_driver_1_f, n7_segment_display_driver_1_g, n7_segment_display_driver_2_a_2,
       n7_segment_display_driver_2_b_2, n7_segment_display_driver_2_c_2, n7_segment_display_driver_2_d_2,
       n7_segment_display_driver_2_e, n7_segment_display_driver_2_f, n7_segment_display_driver_2_g;

  _4bit_To_5bit_BCD u_4bit_to_5bit_bcd_1 (.A(I3), .B(I2), .C(I1), .D(I0), .W(O4), .X(O3), .Y(O2), .Z(O1), .E(O0));
  _4bit_To_5bit_BCD u_4bit_to_5bit_bcd_2 (
    .A(I3_2), .B(I2_2), .C(I1_2), .D(I0_2), .W(n4bit_to_5bit_bcd_2_w), .X(n4bit_to_5bit_bcd_2_x),
    .Y(n4bit_to_5bit_bcd_2_y), .Z(n4bit_to_5bit_bcd_2_z), .E(n4bit_to_5bit_bcd_2_e));
  _7_segment_display_driver u_7_segment_display_driver_1 (
    .D(in_7), .C(in_6), .B(in_5), .A(n4bit_to_5bit_bcd_2_w), .a_2(n7_segment_display_driver_1_a_2),
    .b_2(n7_segment_display_driver_1_b_2), .c_2(n7_segment_display_driver_1_c_2),
    .d_2(n7_segment_display_driver_1_d_2), .e(n7_segment_display_driver_1_e),
    .f(n7_segment_display_driver_1_f), .g(n7_segment_display_driver_1_g));
  _7_segment_display_driver u_7_segment_display_driver_2 (
    .D(n4bit_to_5bit_bcd_2_x), .C(n4bit_to_5bit_bcd_2_y), .B(n4bit_to_5bit_bcd_2_z),
    .A(n4bit_to_5bit_bcd_2_e), .a_2(n7_segment_display_driver_2_a_2), .b_2(n7_segment_display_driver_2_b_2),
    .c_2(n7_segment_display_driver_2_c_2), .d_2(n7_segment_display_driver_2_d_2),
    .e(n7_segment_display_driver_2_e), .f(n7_segment_display_driver_2_f), .g(n7_segment_display_driver_2_g));
  _7_Segment_Display u_7_segment_display_1 (
    .g(n7_segment_display_driver_2_g), .f(n7_segment_display_driver_2_f),
    .a(n7_segment_display_driver_2_a_2), .b(n7_segment_display_driver_2_b_2),
    .e(n7_segment_display_driver_2_e), .d(n7_segment_display_driver_2_d_2),
    .c(n7_segment_display_driver_2_c_2));  // open: dp
  _7_Segment_Display u_7_segment_display_2 (
    .g(n7_segment_display_driver_1_g), .f(n7_segment_display_driver_1_f),
    .a(n7_segment_display_driver_1_a_2), .b(n7_segment_display_driver_1_b_2),
    .e(n7_segment_display_driver_1_e), .d(n7_segment_display_driver_1_d_2),
    .c(n7_segment_display_driver_1_c_2));  // open: dp

  // Notes on the sheet:
  //   BCD TEST
  //   Solution
endmodule

// BCD
module _4bit_To_5bit_BCD (
  input  A,
  input  B,
  input  C,
  input  D,
  output W,
  output X,
  output Y,
  output Z,
  output E
);

  wire and_1_out, and_2_out, and_3_out, and_4_out, and_6_out, and_7_out, not_1_out, not_2_out, not_3_out;

  and and_1 (and_1_out, A, B);
  and and_2 (and_2_out, A, C);
  or or_1 (W, and_1_out, and_2_out);
  not not_1 (not_1_out, B);
  not not_2 (not_2_out, C);
  not not_3 (not_3_out, A);
  and and_3 (and_3_out, not_3_out, B);
  and and_4 (and_4_out, B, C);
  and and_5 (X, A, not_1_out, not_2_out);
  or or_2 (Y, and_3_out, and_4_out);
  and and_6 (and_6_out, not_2_out, B, A);
  or or_3 (Z, and_6_out, and_7_out);
  and and_7 (and_7_out, C, not_3_out);

  assign E = D;
endmodule
