// Logisim project Labwork10_s2_19070001001.circ as structural Verilog: 1 circuit, main circuit main
module main (
);

  wire and_1_out, and_2_out, clock_1_out, j_k_ff_1_q, j_k_ff_2_q, j_k_ff_3_q, main_1_a, main_1_b, main_1_c,
       main_1_d, main_1_e, main_1_f, main_1_g, not_1_out, not_2_out, or_1_out, or_2_out;

  not not_1 (not_1_out, j_k_ff_1_q);
  and and_1 (and_1_out, not_1_out, j_k_ff_2_q);
  Clock clock_1 (.out(clock_1_out));
  and and_2 (and_2_out, j_k_ff_2_q, j_k_ff_3_q);
  or or_1 (or_1_out, j_k_ff_2_q, j_k_ff_3_q);
  not not_2 (not_2_out, j_k_ff_3_q);
  or or_2 (or_2_out, j_k_ff_1_q, j_k_ff_3_q);
  J_K_Flip_Flop j_k_ff_1 (
    .J(and_2_out), .clk(clock_1_out), .K(or_1_out), .Q(j_k_ff_1_q));  // open: Qn, preset, en, reset
  J_K_Flip_Flop j_k_ff_2 (
    .J(not_2_out), .clk(clock_1_out), .K(or_2_out), .Q(j_k_ff_2_q));  // open: Qn, preset, en, reset
  J_K_Flip_Flop j_k_ff_3 (.J(and_1_out), .clk(clock_1_out), .K(1'b1), .Q(j_k_ff_3_q));  // open: Qn, preset, en, reset
  one_bit_driver_main main_1 (
    .Q2(j_k_ff_1_q), .Q1(j_k_ff_2_q), .Q0(j_k_ff_3_q), .a(main_1_a), .b(main_1_b), .c(main_1_c),
    .d(main_1_d), .e(main_1_e), .f(main_1_f), .g(main_1_g));
  _7_Segment_Display u_7_segment_display_1 (
    .g(main_1_g), .f(main_1_f), .a(main_1_a), .b(main_1_b), .e(main_1_e), .d(main_1_d), .c(main_1_c));  // open: dp
endmodule
