// Logisim project latchesffs.circ as structural Verilog: 3 circuits, main circuit JK
module JK (
  input  J,
  input  K,
  input  Set_Reset,
  output out_4,
  output out_5
);

  wire and_1_out, and_2_out, clock_1_out, not_1_out, or_1_out;

  Clock clock_1 (.out(clock_1_out));
  not not_1 (not_1_out, K);
  and and_1 (and_1_out, J, out_5);
  or or_1 (or_1_out, and_1_out, and_2_out);
  and and_2 (and_2_out, not_1_out, out_4);
  DFlipFlopWReset dflipflopwreset_1 (.in_1(or_1_out), .in_2(clock_1_out), .Set_Reset(Set_Reset), .out_4(out_4));
  not not_2 (out_5, out_4);

  // Notes on the sheet:
  //   JK Flip Flop With Set/Reset input
  //   To start JK Flip Flop first you need to Start with Set/Reset input and make CLK 0 to 1
  //   After  the circuit started you have to switch Set/Reset to 0 in order to work properly
endmodule

module DLatch (
  input  D,
  input  E,
  output Q,
  output Q_prime
);

  wire nand_1_out, nand_2_out, not_1_out;

  not not_1 (not_1_out, D);
  nand nand_1 (nand_1_out, D, E);
  nand nand_2 (nand_2_out, not_1_out, E);
  nand nand_3 (Q, nand_1_out, Q_prime);
  nand nand_4 (Q_prime, Q, nand_2_out);

  // Notes on the sheet:
  //   Basic D Latch
endmodule

module DFlipFlopWReset (
  input  in_1,
  input  in_2,
  input  Set_Reset,
  output out_4
);

  wire dlatch_1_q, not_1_out, or_1_out;

  or or_1 (or_1_out, in_1, Set_Reset);
  DLatch dlatch_1 (.D(or_1_out), .E(in_2), .Q(dlatch_1_q));  // open: Q_prime
  not not_1 (not_1_out, in_2);
  DLatch dlatch_2 (.D(dlatch_1_q), .E(not_1_out), .Q(out_4));  // open: Q_prime

  // Notes on the sheet:
  //   D Flip Flop With Set/Reset Input
endmodule
