// Logisim project Labwork11_s2_19070001001.circ as structural Verilog: 1 circuit, main circuit main
module main (
);

  wire and_1_out, and_2_out, and_3_out, and_4_out, clock_1_out, d_ff_1_q, j_k_ff_1_q, j_k_ff_2_q,
       n7_segment_display_driver_1_a_2, n7_segment_display_driver_1_b_2, n7_segment_display_driver_1_c_2,
       n7_segment_display_driver_1_d_2, n7_segment_display_driver_1_e, n7_segment_display_driver_1_f,
       n7_segment_display_driver_1_g, not_1_out, not_2_out, not_3_out, not_4_out, not_5_out, not_6_out,
       or_1_out, t_ff_1_q;

  or or_1 (or_1_out, and_1_out, and_2_out, and_3_out);
  Clock clock_1 (.out(clock_1_out));
  not not_1 (not_1_out, j_k_ff_2_q);
  and and_1 (and_1_out, not_1_out, not_2_out, not_3_out);
  not not_2 (not_2_out, d_ff_1_q);
  not not_3 (not_3_out, t_ff_1_q);
  and and_2 (and_2_out, d_ff_1_q, t_ff_1_q);
  and and_3 (and_3_out, d_ff_1_q, j_k_ff_2_q);
  not not_4 (not_4_out, j_k_ff_2_q);
  not not_5 (not_5_out, d_ff_1_q);
  and and_4 (and_4_out, not_5_out, not_4_out, not_6_out);
  not not_6 (not_6_out, t_ff_1_q);
  J_K_Flip_Flop j_k_ff_1 (
    .J(and_4_out), .clk(clock_1_out), .K(and_4_out), .Q(j_k_ff_1_q));  // open: Qn, preset, en, reset
  D_Flip_Flop d_ff_1 (.clk(clock_1_out), .D(or_1_out), .Q(d_ff_1_q));  // open: Qn, preset, en, reset
  J_K_Flip_Flop j_k_ff_2 (
    .J(not_6_out), .clk(clock_1_out), .K(not_6_out), .Q(j_k_ff_2_q));  // open: Qn, preset, en, reset
  T_Flip_Flop t_ff_1 (.clk(clock_1_out), .T(1'b1), .Q(t_ff_1_q));  // open: Qn, preset, reset, en
  _7_segment_display_driver u_7_segment_display_driver_1 (
    .D(j_k_ff_1_q), .C(d_ff_1_q), .B(j_k_ff_2_q), .A(t_ff_1_q), .a_2(n7_segment_display_driver_1_a_2),
    .b_2(n7_segment_display_driver_1_b_2), .c_2(n7_segment_display_driver_1_c_2),
    .d_2(n7_segment_display_driver_1_d_2), .e(n7_segment_display_driver_1_e),
    .f(n7_segment_display_driver_1_f), .g(n7_segment_display_driver_1_g));
  _7_Segment_Display u_7_segment_display_1 (
    .g(n7_segment_display_driver_1_g), .f(n7_segment_display_driver_1_f),
    .a(n7_segment_display_driver_1_a_2), .b(n7_segment_display_driver_1_b_2),
    .e(n7_segment_display_driver_1_e), .d(n7_segment_display_driver_1_d_2),
    .c(n7_segment_display_driver_1_c_2));  // open: dp
endmodule
