// Logisim project 19070001001_Lab13_s2.circ as structural Verilog: 3 circuits, main circuit main
module main (
);

  wire shiftregcommonclock_1_out_1, shiftregcommonclock_1_out_2;
  wire [7:0] n8_bit_ripple_1_out_1, ram_1_data, shift_register_1_q0, shift_register_1_q1,
       shift_register_1_q2, shift_register_1_q3, shift_register_1_q4, shift_register_1_q5,
       shift_register_1_q6, shift_register_1_q7, shift_register_2_q0, shift_register_2_q1,
       shift_register_2_q2, shift_register_2_q3, shift_register_2_q4, shift_register_2_q5,
       shift_register_2_q6, shift_register_2_q7;

  _8_bit_ripple u_8_bit_ripple_1 (
    .out_1(n8_bit_ripple_1_out_1[0]), .out_2(n8_bit_ripple_1_out_1[1]), .out_3(n8_bit_ripple_1_out_1[2]),
    .out_4(n8_bit_ripple_1_out_1[3]), .out_5(n8_bit_ripple_1_out_1[4]), .out_6(n8_bit_ripple_1_out_1[5]),
    .out_7(n8_bit_ripple_1_out_1[6]), .out_8(n8_bit_ripple_1_out_1[7]));
  ShiftRegCommonClock shiftregcommonclock_1 (.out_1(shiftregcommonclock_1_out_1), .out_2(shiftregcommonclock_1_out_2));
  RAM ram_1 (.addr(n8_bit_ripple_1_out_1), .data(ram_1_data));  // open: sel, clk, ld, clr
  Shift_Register #(.width(8)) shift_register_1 (
    .shift(shiftregcommonclock_1_out_1), .in(ram_1_data), .clk(shiftregcommonclock_1_out_1),
    .q0(shift_register_1_q0), .q1(shift_register_1_q1), .q2(shift_register_1_q2), .q3(shift_register_1_q3),
    .q4(shift_register_1_q4), .q5(shift_register_1_q5), .q6(shift_register_1_q6), .q7(shift_register_1_q7));  // open: out, load, clr, d0, d1, d2, d3, d4, d5, d6, d7
  Shift_Register #(.width(8)) shift_register_2 (
    .clk(shiftregcommonclock_1_out_2), .load(shiftregcommonclock_1_out_2), .d0(shift_register_1_q0),
    .q0(shift_register_2_q0), .d1(shift_register_1_q1), .q1(shift_register_2_q1), .d2(shift_register_1_q2),
    .q2(shift_register_2_q2), .d3(shift_register_1_q3), .q3(shift_register_2_q3), .d4(shift_register_1_q4),
    .q4(shift_register_2_q4), .d5(shift_register_1_q5), .q5(shift_register_2_q5), .d6(shift_register_1_q6),
    .q6(shift_register_2_q6), .d7(shift_register_1_q7), .q7(shift_register_2_q7));  // open: shift, in, out, clr
  DotMatrix #(.inputtype("row"), .matrixcols(8), .matrixrows(8), .persist(16)) dotmatrix_1 (
    .row0(shift_register_2_q7), .row1(shift_register_2_q5), .row2(shift_register_2_q4),
    .row3(shift_register_2_q3), .row4(shift_register_2_q2), .row5(shift_register_2_q1),
    .row6(shift_register_2_q0), .row7(shift_register_2_q6));

  // Notes on the sheet:
  //   bottom output ticks on every 8th top tick
  //   19070001001
endmodule

// 8-bit-RIPP
module _8_bit_ripple (
  output out_1,
  output out_2,
  output out_3,
  output out_4,
  output out_5,
  output out_6,
  output out_7,
  output out_8
);

  wire clock_1_out, d_ff_1_qn, d_ff_2_qn, d_ff_3_qn, d_ff_4_qn, d_ff_5_qn, d_ff_6_qn, d_ff_7_qn, d_ff_8_qn;

  Clock clock_1 (.out(clock_1_out));
  D_Flip_Flop d_ff_1 (.clk(clock_1_out), .D(d_ff_1_qn), .Q(out_1), .Qn(d_ff_1_qn));  // open: preset, en, reset
  D_Flip_Flop d_ff_2 (.clk(d_ff_1_qn), .D(d_ff_2_qn), .Q(out_2), .Qn(d_ff_2_qn));  // open: preset, en, reset
  D_Flip_Flop d_ff_3 (.clk(d_ff_2_qn), .D(d_ff_3_qn), .Q(out_3), .Qn(d_ff_3_qn));  // open: preset, en, reset
  D_Flip_Flop d_ff_4 (.clk(d_ff_3_qn), .D(d_ff_4_qn), .Q(out_4), .Qn(d_ff_4_qn));  // open: preset, en, reset
  D_Flip_Flop d_ff_5 (.clk(d_ff_4_qn), .D(d_ff_5_qn), .Q(out_5), .Qn(d_ff_5_qn));  // open: preset, en, reset
  D_Flip_Flop d_ff_6 (.clk(d_ff_5_qn), .D(d_ff_6_qn), .Q(out_6), .Qn(d_ff_6_qn));  // open: preset, en, reset
  D_Flip_Flop d_ff_7 (.clk(d_ff_6_qn), .D(d_ff_7_qn), .Q(out_7), .Qn(d_ff_7_qn));  // open: preset, en, reset
  D_Flip_Flop d_ff_8 (.clk(d_ff_7_qn), .D(d_ff_8_qn), .Q(out_8), .Qn(d_ff_8_qn));  // open: preset, en, reset
endmodule

// Ticks
module ShiftRegCommonClock (
  output out_1,
  output out_2
);

  wire d_ff_1_q, d_ff_1_qn, d_ff_2_q, d_ff_2_qn, d_ff_3_q, d_ff_3_qn;

  Clock clock_1 (.out(out_1));
  D_Flip_Flop d_ff_1 (.clk(out_1), .D(d_ff_1_qn), .Q(d_ff_1_q), .Qn(d_ff_1_qn));  // open: preset, en, reset
  D_Flip_Flop d_ff_2 (.clk(d_ff_1_qn), .D(d_ff_2_qn), .Q(d_ff_2_q), .Qn(d_ff_2_qn));  // open: preset, en, reset
  D_Flip_Flop d_ff_3 (.clk(d_ff_2_qn), .D(d_ff_3_qn), .Q(d_ff_3_q), .Qn(d_ff_3_qn));  // open: preset, en, reset
  and and_1 (out_2, d_ff_1_q, d_ff_2_q, d_ff_3_q);

  // Notes on the sheet:
  //   Serial Shift Register Reader
  //   Parralel Shift Register Reader
  //   Ticks every 8 clock tick
endmodule
