// Logisim project Labwork4_s2_19070001001.circ as structural Verilog: 1 circuit, main circuit main
module main (
  input  x,
  input  y,
  input  z,
  input  t,
  output F_x_y_z_t______x_prime____x___y_z_y_prime___y_t_prime____x___y_z__z_prime___x___y_prime_zt_prime
);

  wire and_1_out, and_2_out, and_3_out, and_4_out, and_5_out, not_1_out, not_2_out, not_3_out, not_4_out,
       or_1_out, or_2_out, or_3_out, or_4_out;

  or or_1 (or_1_out, x, y);
  not not_1 (not_1_out, t);
  not not_2 (not_2_out, x);
  and and_1 (and_1_out, or_1_out, z);
  or or_2 (or_2_out, not_2_out, and_1_out);
  not not_3 (not_3_out, y);
  or or_3 (or_3_out, and_1_out, not_1_out);
  and and_2 (and_2_out, or_2_out, not_3_out);
  and and_3 (and_3_out, y, or_3_out);
  or or_4 (or_4_out, and_2_out, and_3_out);
  not not_4 (not_4_out, z);
  and and_4 (and_4_out, or_4_out, not_4_out);
  and and_5 (and_5_out, z, not_3_out, not_1_out);
  or or_5 (F_x_y_z_t______x_prime____x___y_z_y_prime___y_t_prime____x___y_z__z_prime___x___y_prime_zt_prime, and_4_out, and_5_out, x);

  // Notes on the sheet:
  //   ((x′ + (x + y)z)y′ + y(t′ + (x + y)z))z′ + x + y′zt′
  //   ((x + y)z)
  //   (x′ + (x + y)z)
  //   (t' + (x + y)z)
  //   (x′ + (x + y)z)y′
  //   y(t' + (x + y)z)
  //   (x′ + (x + y)z)y′ + y(t′ + (x + y)z)
  //   ((x′ + (x + y)z)y′ + y(t′ + (x + y)z))z'
  //   y′zt′
  //   x
endmodule
