// Logisim project Labwork5_s2_19070001001.circ as structural Verilog: 1 circuit, main circuit main
module main (
  input  W,
  input  X,
  input  Y,
  input  Z,
  output out_5
);

  wire and_1_out, and_2_out, and_3_out, and_4_out, not_1_out, not_2_out, not_3_out, not_4_out;

  not not_1 (not_1_out, W);
  not not_2 (not_2_out, Y);
  not not_3 (not_3_out, Z);
  not not_4 (not_4_out, X);
  and and_1 (and_1_out, not_1_out, not_2_out, not_3_out);
  and and_2 (and_2_out, W, X, Z);
  and and_3 (and_3_out, X, Y, not_3_out);
  and and_4 (and_4_out, not_4_out, not_2_out);
  or or_1 (out_5, and_1_out, and_2_out, and_3_out, and_4_out);

  // Notes on the sheet:
  //   x'y'
  //   w'y'z
  //   wxz
  //   xyz'
  //   F(w,x,y,z)= w'y'z' + wxz + x'y' + xyz'
  //   w'y'z' + wxz + x'y' + xyz'
endmodule
