// Logisim project Labwork7_s2_19070001001.circ as structural Verilog: 6 circuits, main circuit main
module main (
  input  A,
  input  A_2,
  input  B,
  input  B_2,
  input  Cinitial,
  input  A0,
  input  A1,
  input  A1_2,
  input  A0_2,
  input  B0,
  input  B1,
  input  B3,
  input  B2,
  input  B1_2,
  input  B0_2,
  input  A3,
  input  A2,
  input  A1_3,
  input  A0_3,
  input  B3_2,
  input  B2_2,
  input  B1_3,
  input  B0_3,
  output S,
  output S_2,
  output C,
  output C_2,
  output D0,
  output D1,
  output D0_2,
  output D2,
  output D1_2,
  output D3,
  output D2_2,
  output D3_2,
  output D0_3,
  output D1_3,
  output D2_3,
  output D3_3,
  output D4,
  output D5,
  output D6,
  output D7
);

  HalfAdder halfadder_1 (.A(A), .B(B_2), .S(S), .C(C));
  _2by2Multiplier u_2by2multiplier_1 (.A(A0), .A1(A1), .B(B0), .B1(B1), .P(D0), .P1(D1), .P2(D2), .P3(D3));
  _4by4Multiplier u_4by4multiplier_1 (
    .A3(A3), .A2(A2), .A1(A1_3), .A(A0_3), .B3(B3_2), .B2(B2_2), .B1(B1_3), .B(B0_3), .C(D0_3), .C1(D1_3),
    .C2(D2_3), .C3(D3_3), .C4(D4), .C5(D5), .C6(D6), .C7(D7));
  FullAdder fulladder_1 (.A(A_2), .B(B), .Carry(Cinitial), .S(S_2), .C(C_2));
  _2bit_4bit_adder u_2bit_4bit_adder_1 (
    .A(A1_2), .A1(A0_2), .B3(B3), .B2(B2), .B1(B1_2), .B(B0_2), .C(D0_2), .C1(D1_2), .C2(D2_2), .C3(D3_2));

  // Notes on the sheet:
  //   1- Half Adder
  //   3- 2 bit by 2 bit Multiplier
  //   Subcircuit Tests
  //   5- 4 bit by 4 bit Multiplier
  //   2- Full Adder
  //   4- 2 bit + 4 bit Adder
endmodule

// HA
module HalfAdder (
  input  A,
  input  B,
  output S,
  output C
);

  xor xor_1 (S, A, B);
  and and_1 (C, A, B);
endmodule

// FA
module FullAdder (
  input  A,
  input  B,
  input  Carry,
  output S,
  output C
);

  wire halfadder_1_c, halfadder_1_s, halfadder_2_c;

  HalfAdder halfadder_1 (.A(A), .B(B), .S(halfadder_1_s), .C(halfadder_1_c));
  HalfAdder halfadder_2 (.A(halfadder_1_s), .B(Carry), .S(S), .C(halfadder_2_c));
  or or_1 (C, halfadder_2_c, halfadder_1_c);
endmodule

// 2x2
module _2by2Multiplier (
  input  A,
  input  A1,
  input  B,
  input  B1,
  output P,
  output P1,
  output P2,
  output P3
);

  wire and_2_out, and_3_out, and_4_out, halfadder_1_c;

  and and_1 (P, A, B);
  and and_2 (and_2_out, A1, B);
  and and_3 (and_3_out, A, B1);
  and and_4 (and_4_out, A1, B1);
  HalfAdder halfadder_1 (.A(and_2_out), .B(and_3_out), .S(P1), .C(halfadder_1_c));
  HalfAdder halfadder_2 (.A(halfadder_1_c), .B(and_4_out), .S(P2), .C(P3));
endmodule

// 2b+4b
module _2bit_4bit_adder (
  input  A,
  input  A1,
  input  B3,
  input  B2,
  input  B1,
  input  B,
  output C,
  output C1,
  output C2,
  output C3
);

  wire fulladder_1_c, halfadder_1_c, halfadder_2_c;

  HalfAdder halfadder_1 (.A(A1), .B(B), .S(C), .C(halfadder_1_c));
  FullAdder fulladder_1 (.A(halfadder_1_c), .B(A), .Carry(B1), .S(C1), .C(fulladder_1_c));
  HalfAdder halfadder_2 (.A(fulladder_1_c), .B(B2), .S(C2), .C(halfadder_2_c));
  HalfAdder halfadder_3 (.A(halfadder_2_c), .B(B3), .S(C3));  // open: C
endmodule

// 4x4
module _4by4Multiplier (
  input  A3,
  input  A2,
  input  A1,
  input  A,
  input  B3,
  input  B2,
  input  B1,
  input  B,
  output C,
  output C1,
  output C2,
  output C3,
  output C4,
  output C5,
  output C6,
  output C7
);

  wire n2bit_4bit_adder_1_c, n2bit_4bit_adder_1_c1, n2bit_4bit_adder_1_c2, n2bit_4bit_adder_1_c3,
       n2bit_4bit_adder_2_c, n2bit_4bit_adder_2_c1, n2bit_4bit_adder_2_c2, n2bit_4bit_adder_2_c3,
       n2bit_4bit_adder_3_c2, n2bit_4bit_adder_3_c3, n2by2multiplier_1_p2, n2by2multiplier_1_p3,
       n2by2multiplier_2_p, n2by2multiplier_2_p1, n2by2multiplier_2_p2, n2by2multiplier_2_p3,
       n2by2multiplier_3_p, n2by2multiplier_3_p1, n2by2multiplier_3_p2, n2by2multiplier_3_p3,
       n2by2multiplier_4_p, n2by2multiplier_4_p1, n2by2multiplier_4_p2, n2by2multiplier_4_p3;

  _2by2Multiplier u_2by2multiplier_1 (
    .A(A), .A1(A1), .B(B), .B1(B1), .P(C), .P1(C1), .P2(n2by2multiplier_1_p2), .P3(n2by2multiplier_1_p3));
  _2by2Multiplier u_2by2multiplier_2 (
    .A(A), .A1(A1), .B(B2), .B1(B3), .P(n2by2multiplier_2_p), .P1(n2by2multiplier_2_p1),
    .P2(n2by2multiplier_2_p2), .P3(n2by2multiplier_2_p3));
  _2by2Multiplier u_2by2multiplier_3 (
    .A(A2), .A1(A3), .B(B), .B1(B1), .P(n2by2multiplier_3_p), .P1(n2by2multiplier_3_p1),
    .P2(n2by2multiplier_3_p2), .P3(n2by2multiplier_3_p3));
  _2by2Multiplier u_2by2multiplier_4 (
    .A(A2), .A1(A3), .B(B2), .B1(B3), .P(n2by2multiplier_4_p), .P1(n2by2multiplier_4_p1),
    .P2(n2by2multiplier_4_p2), .P3(n2by2multiplier_4_p3));
  _2bit_4bit_adder u_2bit_4bit_adder_1 (
    .A(n2by2multiplier_1_p3), .A1(n2by2multiplier_1_p2), .B3(n2by2multiplier_2_p3),
    .B2(n2by2multiplier_2_p2), .B1(n2by2multiplier_2_p1), .B(n2by2multiplier_2_p), .C(n2bit_4bit_adder_1_c),
    .C1(n2bit_4bit_adder_1_c1), .C2(n2bit_4bit_adder_1_c2), .C3(n2bit_4bit_adder_1_c3));
  _2bit_4bit_adder u_2bit_4bit_adder_2 (
    .A(n2by2multiplier_3_p3), .A1(n2by2multiplier_3_p2), .B3(n2by2multiplier_4_p3),
    .B2(n2by2multiplier_4_p2), .B1(n2by2multiplier_4_p1), .B(n2by2multiplier_4_p), .C(n2bit_4bit_adder_2_c),
    .C1(n2bit_4bit_adder_2_c1), .C2(n2bit_4bit_adder_2_c2), .C3(n2bit_4bit_adder_2_c3));
  _2bit_4bit_adder u_2bit_4bit_adder_3 (
    .A(n2by2multiplier_3_p1), .A1(n2by2multiplier_3_p), .B3(n2bit_4bit_adder_1_c3),
    .B2(n2bit_4bit_adder_1_c2), .B1(n2bit_4bit_adder_1_c1), .B(n2bit_4bit_adder_1_c), .C(C2), .C1(C3),
    .C2(n2bit_4bit_adder_3_c2), .C3(n2bit_4bit_adder_3_c3));
  _2bit_4bit_adder u_2bit_4bit_adder_4 (
    .A(n2bit_4bit_adder_3_c3), .A1(n2bit_4bit_adder_3_c2), .B3(n2bit_4bit_adder_2_c3),
    .B2(n2bit_4bit_adder_2_c2), .B1(n2bit_4bit_adder_2_c1), .B(n2bit_4bit_adder_2_c), .C(C4), .C1(C5),
    .C2(C6), .C3(C7));
endmodule
