// Logisim project lab02.circ as structural Verilog: 1 circuit, main circuit main
module main (
  input  A,
  input  B,
  output Y,
  output Y_2,
  output Y_3,
  output Y_4,
  output Y_5,
  output Y_6
);

  and and_1 (Y, A, B);
  or or_1 (Y_3, A, B);
  not not_1 (Y_5, A);
  nand nand_1 (Y_2, A, B);
  nor nor_1 (Y_4, A, B);
  xor xor_1 (Y_6, A, B);
endmodule
